# Fritzing sketch sketch (saved by Fritzing 0.9.3b)
breadboards: 1

parts:
  Part1 = Arduino Uno (Rev3)
  LED1 = smd LED [color="Red (633nm)" package="0805 [SMD]"]
  LED2 = smd LED [color="Red (633nm)" package="0805 [SMD]"]
  LED3 = smd LED [color="Red (633nm)" package="0805 [SMD]"]
  LED4 = smd LED [color="Red (633nm)" package="0805 [SMD]"]
  R1 = Resistor [tolerance=±5% resistance=220 package="2512 [SMD]"]
  R2 = Resistor [tolerance=±5% resistance=220 package="2512 [SMD]"]
  R3 = Resistor [tolerance=±5% resistance=220 package="2512 [SMD]"]
  R4 = Resistor [tolerance=±5% resistance=220 package="2512 [SMD]"]
  LED5 = smd LED [color="Red (633nm)" package="0805 [SMD]"]
  R5 = Resistor [tolerance=±5% resistance=220 package="2512 [SMD]"]
  S1 = Pushbutton [package="[THT]"]
  R6 = Resistor [tolerance=±5% resistance=10k package="2512 [SMD]"]
  SG1 = Buzzer 12mm [package=buzzer-12mm-ns]
  Part2 = Breakout Board for Electret Microphone
  S2 = Pushbutton [package="[THT]"]
  R7 = Resistor [tolerance=±5% resistance=10k package="2512 [SMD]"]

nets:
  N1: Part1.A0, Part2.VCC
  N2: Part1.D8, S1.Pin_1, S1.Pin_2, R6.Pin_0
  N3: Part1.D9_PWM, SG1.1
  N4: Part1.D10_PWM/SS, S2.Pin_1, S2.Pin_2, R7.Pin_0
  N5: Part1.GND, R1.Pin_1, R2.Pin_1, R3.Pin_1, R4.Pin_1, R5.Pin_1, R6.Pin_1, SG1.2, Part2.AUD, R7.Pin_1
  N6: Part1.D2, LED1.anode
  N7: Part1.D3_PWM, LED2.cathode
  N8: Part1.D4, LED3.cathode
  N9: Part1.D5_PWM, LED4.cathode
  N10: Part1.D6_PWM, LED5.cathode
  N11: LED1.cathode, R1.Pin_0
  N12: LED2.anode, R2.Pin_0
  N13: LED3.anode, R3.Pin_0
  N14: LED4.anode, R4.Pin_0
  N15: LED5.anode, R5.Pin_0
  N16: S1.Pin_3, S1.Pin_4, Part2.GND, S2.Pin_3, S2.Pin_4
